// Logisim project 01.labTask.Components.circ as structural Verilog: 8 circuits, main circuit main
module main (
);

  AddMachine addmachine_1 ();  // open: out_1, out_2
endmodule

module NAND (
  input  in_1,
  input  in_2,
  output out_3
);

  wire and_1_out;

  and and_1 (and_1_out, in_1, in_2);
  not not_1 (out_3, and_1_out);
endmodule

module NOR (
  input  in_1,
  input  in_2,
  output out_3
);

  wire or_1_out;

  or or_1 (or_1_out, in_1, in_2);
  not not_1 (out_3, or_1_out);
endmodule

module XOR_fb4a8bfb (
  input  in_1,
  input  in_2,
  output out_3
);

  wire and_1_out, and_2_out, not_1_out, not_2_out;

  not not_1 (not_1_out, in_1);
  not not_2 (not_2_out, in_2);
  and and_1 (and_1_out, in_1, not_2_out);
  and and_2 (and_2_out, not_1_out, in_2);
  or or_1 (out_3, and_1_out, and_2_out);
endmodule

module MUX_2x1 (
  input  in_1,
  input  in_2,
  input  in_3,
  output out_4
);

  wire and_1_out, and_2_out, not_1_out;

  not not_1 (not_1_out, in_3);
  and and_1 (and_1_out, in_1, in_3);
  and and_2 (and_2_out, in_2, not_1_out);
  or or_1 (out_4, and_1_out, and_2_out);
endmodule

module MUX_4x1 (
  input  I0,
  input  I1,
  input  I2,
  input  I3,
  input  S0,
  input  S1,
  output O
);

  wire mux_2x1_1_out_4, mux_2x1_2_out_4;

  MUX_2x1 mux_2x1_1 (.in_1(I0), .in_2(I1), .in_3(S0), .out_4(mux_2x1_1_out_4));
  MUX_2x1 mux_2x1_2 (.in_1(I2), .in_2(I3), .in_3(S1), .out_4(mux_2x1_2_out_4));
  or or_1 (O, mux_2x1_1_out_4, mux_2x1_2_out_4);
endmodule

module AddMachine (
  output [7:0] out_1,
  output [7:0] out_2
);

  wire clock_1_out;

  Clock clock_1 (.out(clock_1_out));
  Adder adder_1 (.a(out_2), .b(8'h1), .out(out_1));  // open: cin, cout
  Register register_1 (.D(out_1), .Q(out_2), .clk(clock_1_out));  // open: en, clr
endmodule

module Ex4 (
  input  [7:0] In,
  output Out1,
  output [7:0] Out2
);

  Bit_Extender #(.out_width(7)) bit_extender_1 (.in(In), .out(Out2[6:0]));
  and and_1 (Out1, In[0], In[7]);

  assign Out2[7] = 1'b1;
endmodule
