// Logisim project 32BitCPU.circ as structural Verilog: 16 circuits, main circuit main
module main (
  output [31:0] REG_rs1,
  output [31:0] REG_rs2,
  output [31:0] Memory_Read,
  output [31:0] ALU_out,
  output [31:0] Ins,
  output [31:0] Imm32
);

  wire ASel, BrEq, BrLt, BSel, controlpath_1_brun, MemRW, PCSel, RegEn, SysClk;
  wire [1:0] WBSel;
  wire [2:0] ImmSel;
  wire [3:0] ALUSel;
  wire [4:0] AddrD1, AddrD2, AddrD3;
  wire [15:0] adder_1_out, bit_extender_1_out, PC, PCplus4;
  wire [31:0] alu_1_result, bit_extender_3_out, dataB2, imem_1_instruction, immgen_1_immediatefinal32,
       multiplexer_2_out, multiplexer_3_out, multiplexer_4_out, PC32, rdData, regfile_1_readdata1,
       regfile_1_readdata2;

  Clock clk (.out(SysClk));
  Clock u_sysclk ();  // open: out
  Adder #(.width(16)) adder_1 (.a(PC), .b(16'h1), .out(adder_1_out));  // open: cin, cout
  Bit_Extender #(.in_width(32)) bit_extender_1 (.in(ALU_out), .out(bit_extender_1_out));
  Register #(.width(16)) r0 (.D(PCplus4), .clk(SysClk), .Q(PC));  // open: en, clr
  assign PC32 = {{16{PC[15]}}, PC};  // Bit_Extender bit_extender_2
  Multiplexer #(.width(16), .enable("false")) multiplexer_1 (
    .in0(adder_1_out), .in1(bit_extender_1_out), .out(PCplus4), .sel(PCSel));
  iMem imem_1 (.PCVal(PC), .Instruction(imem_1_instruction));
  Reg_IFID reg_ifid_1 (.Instrction_IN(imem_1_instruction), .Clock_IN(SysClk), .Instruction_OUT(Ins));
  controlPath controlpath_1 (
    .BrEq(BrEq), .BrLt(BrLt), .PCSel(PCSel), .ImmSel(ImmSel), .BrUn(controlpath_1_brun), .ASel(ASel),
    .BSel(BSel), .ALUSel(ALUSel), .MemRW(MemRW), .RegWEn(RegEn), .WBSel(WBSel), .Instruction(Ins),
    .SysClk(SysClk));  // open: out_15, Flasher
  regFile regfile_1 (
    .Clock(SysClk), .RegWEn(RegEn), .rs1(Ins[19:15]), .rs2(Ins[24:20]), .rd(AddrD3), .data(rdData),
    .ReadData2(regfile_1_readdata2), .ReadData1(regfile_1_readdata1));  // open: spVal, t1Val, s0Val, a0Val, raVal, t0Val, t2Val, s1Val
  immGen immgen_1 (.ImmediateFinal32(immgen_1_immediatefinal32), .Instruction(Ins), .ImmSel(ImmSel));  // open: InsType
  Reg_IDEX reg_idex_1 (
    .in_1(Ins[11:7]), .in_2(regfile_1_readdata1), .in_3(regfile_1_readdata2),
    .in_4(immgen_1_immediatefinal32), .in_5(SysClk), .out_6(AddrD1), .out_7(REG_rs1), .out_8(REG_rs2),
    .out_9(Imm32));
  Multiplexer #(.width(32), .enable("false")) multiplexer_2 (
    .in0(REG_rs1), .in1(PC32), .out(multiplexer_2_out), .sel(ASel));
  Multiplexer #(.width(32), .enable("false")) multiplexer_3 (
    .in0(REG_rs2), .in1(Imm32), .out(multiplexer_3_out), .sel(BSel));
  Comparator #(.width(32)) comparator_1 (.a(REG_rs1), .b(REG_rs2), .eq(BrEq), .lt(BrLt));  // open: gt
  ALU alu_1 (.A(multiplexer_2_out), .B(multiplexer_3_out), .ALUSel(ALUSel), .Result(alu_1_result));
  Reg_EXME reg_exme_1 (
    .in_1(alu_1_result), .in_2(REG_rs2), .in_3(AddrD1), .in_4(SysClk), .out_5(ALU_out), .out_6(dataB2),
    .out_7(AddrD2));
  dataMemory datamemory_1 (.MemRW(MemRW), .AddrW(ALU_out), .DataW(dataB2), .SysClk(SysClk), .DataR(Memory_Read));
  assign bit_extender_3_out = {{16{PCplus4[15]}}, PCplus4};  // Bit_Extender bit_extender_3
  Multiplexer #(.select(2), .width(32), .enable("false")) multiplexer_4 (
    .in0(ALU_out), .in1(Memory_Read), .in2(bit_extender_3_out), .out(multiplexer_4_out), .sel(WBSel));  // open: in3
  Reg_MEWB reg_mewb_1 (
    .in_1(AddrD2), .in_3(multiplexer_4_out), .in_4(SysClk), .out_5(AddrD3), .out_6(rdData));  // open: in_2

  // Other names for the same wires on the sheet: ALUout[31:0] = ALU_out; dataA[31:0] = REG_rs1; dataB[31:0] = REG_rs2;
  //   dataR[31:0] = Memory_Read; Inst[31:0] = Ins; OPCODE[6:0] = Ins[6:0]; AddrD[4:0] = Ins[11:7];
  //   AddrA[4:0] = Ins[19:15]; AddrB[4:0] = Ins[24:20]
endmodule

module ALU (
  input  [31:0] A,
  input  [31:0] B,
  input  [3:0] ALUSel,
  output [31:0] Result
);

  wire comparator_1_lt;
  wire [4:0] bit_extender_1_out, bit_extender_2_out, bit_extender_3_out;
  wire [30:0] bit_extender_4_out, bit_extender_5_out;
  wire [30:1] multiplier_1_cout;
  wire [31:0] adder_1_out, and_1_out, bit_extender_6_out, bit_extender_7_out, divider_1_out, divider_1_rem,
       multiplier_1_out, or_1_out, shifter_1_out, shifter_2_out, shifter_3_out, subtractor_1_out, xor_1_out;

  Bit_Extender #(.in_width(32), .out_width(5)) bit_extender_1 (.in(B), .out(bit_extender_1_out));
  Bit_Extender #(.in_width(32), .out_width(5)) bit_extender_2 (.in(B), .out(bit_extender_2_out));
  Bit_Extender #(.in_width(32), .out_width(5)) bit_extender_3 (.in(B), .out(bit_extender_3_out));
  Bit_Extender #(.in_width(32), .out_width(31)) bit_extender_4 (.in(A), .out(bit_extender_4_out));
  Bit_Extender #(.in_width(32), .out_width(31)) bit_extender_5 (.in(B), .out(bit_extender_5_out));
  Comparator #(.width(32)) comparator_1 (.a(A), .b(B), .lt(comparator_1_lt));  // open: gt, eq
  Multiplier #(.width(31)) multiplier_1 (
    .a(bit_extender_4_out), .b(bit_extender_5_out), .out(multiplier_1_out[30:0]),
    .cout({multiplier_1_cout, multiplier_1_out[31]}));  // open: cin
  Adder #(.width(32)) adder_1 (.a(A), .b(B), .out(adder_1_out));  // open: cin, cout
  assign and_1_out = A & B;  // AND_Gate and_1, 32 bits wide
  assign or_1_out = A | B;  // OR_Gate or_1, 32 bits wide
  assign xor_1_out = A ^ B;  // XOR_Gate xor_1, 32 bits wide
  Shifter #(.width(32), .shift("lr")) shifter_1 (.in(A), .\dist (bit_extender_1_out), .out(shifter_1_out));
  Shifter #(.width(32), .shift("ar")) shifter_2 (.in(A), .\dist (bit_extender_2_out), .out(shifter_2_out));
  Shifter #(.width(32)) shifter_3 (.in(A), .\dist (bit_extender_3_out), .out(shifter_3_out));
  assign bit_extender_6_out = {{31{comparator_1_lt}}, comparator_1_lt};  // Bit_Extender bit_extender_6
  Divider #(.width(32)) divider_1 (.a(A), .b(B), .out(divider_1_out), .rem(divider_1_rem));  // open: upper
  assign bit_extender_7_out = {{2{multiplier_1_cout[30]}}, multiplier_1_cout};  // Bit_Extender bit_extender_7
  Subtractor #(.width(32)) subtractor_1 (.a(A), .b(B), .out(subtractor_1_out));  // open: bin, bout
  Multiplexer #(.select(4), .width(32), .enable("false")) multiplexer_1 (
    .in0(adder_1_out), .in1(and_1_out), .in2(or_1_out), .in3(xor_1_out), .in4(shifter_1_out),
    .in5(shifter_2_out), .in6(shifter_3_out), .in7(bit_extender_6_out), .in8(divider_1_out),
    .in9(divider_1_rem), .in10(multiplier_1_out), .in11(bit_extender_7_out), .in12(subtractor_1_out),
    .in13(B), .out(Result), .sel(ALUSel));  // open: in14, in15
endmodule

module regFile (
  input  Clock,
  input  RegWEn,
  input  [4:0] rs1,
  input  [4:0] rs2,
  input  [4:0] rd,
  input  [31:0] data,
  output [31:0] ReadData1,
  output [31:0] ReadData2,
  output [31:0] raVal,
  output [31:0] spVal,
  output [31:0] t0Val,
  output [31:0] t1Val,
  output [31:0] t2Val,
  output [31:0] s0Val,
  output [31:0] s1Val,
  output [31:0] a0Val
);

  wire wr2, wr3, wr4, wr5, wr6, wr7, wr8, wr9;
  wire [31:0] x0;

  Demultiplexer #(.select(5), .enable("false")) demultiplexer_1 (
    .out1(wr2), .out2(wr3), .out5(wr4), .out6(wr5), .out7(wr6), .out8(wr7), .out9(wr8), .out10(wr9),
    .in(1'b1), .sel(rd));  // open: out0, out3, out4, out11, out12, out13, out14, out15, out16, out17, out18, out19, out20, out21, out22, out23, out24, out25, out26, out27, out28, out29, out30, out31
  Register #(.width(32)) register_1 (.D(data), .en(1'b0), .clk(Clock), .Q(x0));  // open: clr
  Register #(.width(32)) register_2 (.D(data), .en(wr4), .clk(Clock), .Q(t0Val));  // open: clr
  Register #(.width(32)) register_3 (.D(data), .en(wr7), .clk(Clock), .Q(s0Val));  // open: clr
  Register #(.width(32)) register_4 (.D(data), .en(wr2), .clk(Clock), .Q(raVal));  // open: clr
  Register #(.width(32)) register_5 (.D(data), .en(wr5), .clk(Clock), .Q(t1Val));  // open: clr
  Register #(.width(32)) register_6 (.D(data), .en(wr8), .clk(Clock), .Q(s1Val));  // open: clr
  Multiplexer #(.select(5), .width(32), .enable("false")) multiplexer_1 (
    .in0(x0), .in1(raVal), .in2(spVal), .in5(t0Val), .in6(t1Val), .in7(t2Val), .in8(s0Val), .in9(s1Val),
    .in10(a0Val), .out(ReadData1), .sel(rs1));  // open: in3, in4, in11, in12, in13, in14, in15, in16, in17, in18, in19, in20, in21, in22, in23, in24, in25, in26, in27, in28, in29, in30, in31
  Register #(.width(32)) register_7 (.D(data), .en(wr3), .clk(Clock), .Q(spVal));  // open: clr
  Register #(.width(32)) register_8 (.D(data), .en(wr6), .clk(Clock), .Q(t2Val));  // open: clr
  Register #(.width(32)) register_9 (.D(data), .en(wr9), .clk(Clock), .Q(a0Val));  // open: clr
  Multiplexer #(.select(5), .width(32), .enable("false")) multiplexer_2 (
    .in0(x0), .in1(raVal), .in2(spVal), .in5(t0Val), .in6(t1Val), .in7(t2Val), .in8(s0Val), .in9(s1Val),
    .in10(a0Val), .out(ReadData2), .sel(rs2));  // open: in3, in4, in11, in12, in13, in14, in15, in16, in17, in18, in19, in20, in21, in22, in23, in24, in25, in26, in27, in28, in29, in30, in31

  // Other names for the same wires on the sheet: regClk = Clock; regDataWrite[31:0] = data; regRDSelect[4:0] = rd;
  //   regRS1Select[4:0] = rs1; regRS2Select[4:0] = rs2; RS1Data[31:0] = ReadData1; RS2Data[31:0] = ReadData2;
  //   x1[31:0] = raVal; x2[31:0] = spVal; x5[31:0] = t0Val; x6[31:0] = t1Val; x7[31:0] = t2Val; x8[31:0] = s0Val;
  //   x9[31:0] = s1Val; x10[31:0] = a0Val

  // Notes on the sheet:
  //   INPUTS
  //   OUTPUTS
endmodule

module iMem (
  input  [15:0] PCVal,
  output [31:0] Instruction
);

  ROM #(.addrWidth(16), .dataWidth(32)) rom_1 (.addr(PCVal), .data(Instruction));

  // Notes on the sheet:
  //   contents of rom_1 (hex, n*v repeats v):
  //   0 508093 202103
endmodule

module controlPath (
  input  BrEq,
  input  BrLt,
  input  [31:0] Instruction,
  input  SysClk,
  input  [15:0] Flasher,
  output PCSel,
  output [2:0] ImmSel,
  output BrUn,
  output ASel,
  output BSel,
  output [3:0] ALUSel,
  output MemRW,
  output RegWEn,
  output [1:0] WBSel,
  output [15:0] out_15
);

  wire reg_1x_1_out_3, reg_1x_2_out_3, reg_1x_3_out_3, reg_1x_4_out_3;
  wire [1:0] reg_2x_1_out_3, reg_2x_2_out_3;
  wire [7:0] bit_extender_1_out, bit_extender_2_out;
  wire [15:0] rom_1_data;

  Bit_Extender #(.in_width(7), .out_width(8), .\type ("zero")) bit_extender_1 (.out(bit_extender_1_out));  // open: in
  assign bit_extender_2_out = {{5{1'b0}}, Instruction[14:12]};  // Bit_Extender bit_extender_2
  Adder adder_1 (.a(bit_extender_1_out), .b(bit_extender_2_out));  // open: out, cin, cout
  assign out_15 = {{5{Instruction[30]}}, {Instruction[30], Instruction[14:12], Instruction[6:2], BrEq, BrLt}};  // Bit_Extender bit_extender_3
  ROM #(.addrWidth(16), .dataWidth(16)) rom_1 (
    .addr(out_15), .data({rom_1_data[15], PCSel, rom_1_data[13:11], BrUn, rom_1_data[9:0]}));
  Reg_2x reg_2x_1 (.in_1(reg_2x_2_out_3), .Clock(SysClk), .out_3(reg_2x_1_out_3));
  Reg_2x reg_2x_2 (.in_1(rom_1_data[1:0]), .Clock(SysClk), .out_3(reg_2x_2_out_3));
  Reg_1x reg_1x_1 (.in_1(rom_1_data[2]), .Clock(SysClk), .out_3(reg_1x_1_out_3));
  Reg_1x reg_1x_2 (.in_1(reg_1x_1_out_3), .Clock(SysClk), .out_3(reg_1x_2_out_3));
  Reg_1x reg_1x_3 (.in_1(rom_1_data[3]), .Clock(SysClk), .out_3(reg_1x_3_out_3));
  Reg_1x reg_1x_4 (.in_1(reg_1x_3_out_3), .Clock(SysClk), .out_3(reg_1x_4_out_3));
  Reg_4x reg_4x_1 (.in_2(SysClk));  // open: in_1, out_3
  Reg_4x reg_4x_2 (.in_1(rom_1_data[7:4]), .in_2(SysClk), .out_3(ALUSel));
  Reg_1x reg_1x_5 (.Clock(SysClk));  // open: in_1, out_3
  Reg_1x reg_1x_6 (.in_1(rom_1_data[8]), .Clock(SysClk), .out_3(BSel));
  Reg_1x reg_1x_7 (.Clock(SysClk));  // open: in_1, out_3
  Reg_1x reg_1x_8 (.in_1(rom_1_data[9]), .Clock(SysClk), .out_3(ASel));
  Reg_3x reg_3x_1 (.in_1(rom_1_data[13:11]), .Clock(SysClk), .out_3(ImmSel));
  Reg_2x reg_2x_3 (.in_1(reg_2x_1_out_3), .Clock(SysClk), .out_3(WBSel));
  Reg_1x reg_1x_9 (.in_1(reg_1x_2_out_3), .Clock(SysClk), .out_3(RegWEn));
  Reg_1x reg_1x_10 (.in_1(reg_1x_4_out_3), .Clock(SysClk), .out_3(MemRW));

  // Other names for the same wires on the sheet: opcode5[4:0] = Instruction[6:2]; func3[2:0] = Instruction[14:12];
  //   b30 = Instruction[30]; Clk = SysClk

  // Notes on the sheet:
  //   contents of rom_1 (hex, n*v repeats v):
  //   4*0 104 0 0 0 4*105 4 0 0 0 4*104 236*0 4*105 772*0 4*105 4*0 4*104 236*0 4*105
endmodule

module dataMemory (
  input  MemRW,
  input  [31:0] AddrW,
  input  [31:0] DataW,
  input  SysClk,
  output [31:0] DataR
);

  wire not_1_out;
  wire [15:0] AddrW_t;
  wire [31:0] ram_1_data;

  Bit_Extender #(.in_width(32)) bit_extender_1 (.in(AddrW), .out(AddrW_t));
  RAM #(.addrWidth(16), .dataWidth(32)) ram_1 (
    .addr(AddrW_t), .we(MemRW), .oe(not_1_out), .clk(SysClk), .data(ram_1_data));
  not not_1 (not_1_out, MemRW);
  Multiplexer #(.width(32), .enable("false")) multiplexer_1 (.in1(DataW), .out(ram_1_data), .sel(MemRW));  // open: in0
  Demultiplexer #(.width(32), .enable("false")) demultiplexer_1 (
    .out0(DataR), .in(ram_1_data), .sel(MemRW));  // open: out1
endmodule

module decodeInst (
  input  [6:0] OPCODE,
  output L,
  output I,
  output I_wide,
  output S,
  output R_add,
  output R_sub,
  output SB,
  output [6:0] InsType
);

  wire not_1_out, not_2_out, not_3_out, not_4_out, not_5_out, not_6_out, not_7_out, not_8_out, not_9_out,
       not_10_out, not_11_out, not_12_out, not_13_out, not_14_out, not_15_out, not_16_out, not_17_out,
       not_18_out, not_19_out, not_20_out, not_21_out, not_22_out, not_23_out, not_24_out;

  not not_1 (not_1_out, OPCODE[2]);
  not not_2 (not_2_out, OPCODE[3]);
  not not_3 (not_3_out, OPCODE[4]);
  not not_4 (not_4_out, OPCODE[5]);
  not not_5 (not_5_out, OPCODE[6]);
  not not_6 (not_6_out, OPCODE[2]);
  not not_7 (not_7_out, OPCODE[3]);
  not not_8 (not_8_out, OPCODE[5]);
  not not_9 (not_9_out, OPCODE[6]);
  not not_10 (not_10_out, OPCODE[2]);
  not not_11 (not_11_out, OPCODE[5]);
  not not_12 (not_12_out, OPCODE[6]);
  not not_13 (not_13_out, OPCODE[2]);
  not not_14 (not_14_out, OPCODE[3]);
  not not_15 (not_15_out, OPCODE[4]);
  not not_16 (not_16_out, OPCODE[6]);
  not not_17 (not_17_out, OPCODE[2]);
  not not_18 (not_18_out, OPCODE[3]);
  not not_19 (not_19_out, OPCODE[6]);
  not not_20 (not_20_out, OPCODE[2]);
  not not_21 (not_21_out, OPCODE[6]);
  not not_22 (not_22_out, OPCODE[2]);
  not not_23 (not_23_out, OPCODE[3]);
  not not_24 (not_24_out, OPCODE[4]);
  and and_1 (InsType[0], not_1_out, not_2_out, not_3_out, not_4_out, not_5_out);
  and and_2 (I, not_6_out, not_7_out, OPCODE[4], not_8_out, not_9_out);
  and and_3 (I_wide, not_10_out, OPCODE[3], OPCODE[4], not_11_out, not_12_out);
  and and_4 (InsType[3], not_13_out, not_14_out, not_15_out, OPCODE[5], not_16_out);
  and and_5 (InsType[4], not_17_out, not_18_out, OPCODE[4], OPCODE[5], not_19_out);
  and and_6 (InsType[5], not_20_out, OPCODE[3], OPCODE[4], OPCODE[5], not_21_out);
  and and_7 (InsType[6], not_22_out, not_23_out, not_24_out, OPCODE[5], OPCODE[6]);

  assign InsType[2:1] = {I_wide, I};
  assign L = InsType[0];
  assign R_add = InsType[4];
  assign R_sub = InsType[5];
  assign S = InsType[3];
  assign SB = InsType[6];
endmodule

module immGen (
  input  [31:0] Instruction,
  input  [2:0] ImmSel,
  input  [6:0] InsType,
  output [31:0] ImmediateFinal32
);

  wire [2:0] InsID;
  wire [31:0] Imm_I, Imm_S, Imm_SB;

  Priority_Encoder priority_encoder_1 (
    .in0(InsType[0]), .in1(InsType[1]), .in2(InsType[2]), .in3(InsType[3]), .in4(InsType[4]),
    .in5(InsType[5]), .in6(InsType[6]), .out(InsID), .en_in(1'b1));  // open: in7, gs, en_out
  assign Imm_I = {{20{1'b0}}, Instruction[31:20]};  // Bit_Extender bit_extender_1
  assign Imm_S = {{20{1'b0}}, {Instruction[31:25], Instruction[11:7]}};  // Bit_Extender bit_extender_2
  assign Imm_SB = {{19{1'b0}}, {Instruction[31], Instruction[7], Instruction[30:25], Instruction[11:8], 1'b0}};  // Bit_Extender bit_extender_3
  Multiplexer #(.select(3), .width(32), .enable("false")) multiplexer_1 (
    .in0(Imm_I), .in1(Imm_S), .in2(Imm_SB), .in3({Instruction[31:12], {12{1'b0}}}), .out(ImmediateFinal32),
    .sel(ImmSel));  // open: in4, in5, in6, in7

  // Other names for the same wires on the sheet: rd[4:0] = Instruction[11:7]; func3[2:0] = Instruction[14:12];
  //   Imm_U[31:12] = Instruction[31:12]; rs1[4:0] = Instruction[19:15]; rs2[4:0] = Instruction[24:20];
  //   func7[6:0] = Instruction[31:25]; opcode[6:0] = Instruction[6:0]
endmodule

module Reg_IFID (
  input  [31:0] Instrction_IN,
  input  Clock_IN,
  output [31:0] Instruction_OUT
);

  Register #(.width(32)) register_1 (.D(Instrction_IN), .en(1'b1), .clk(Clock_IN), .Q(Instruction_OUT));  // open: clr
endmodule

module Reg_IDEX (
  input  [4:0] in_1,
  input  [31:0] in_2,
  input  [31:0] in_3,
  input  [31:0] in_4,
  input  in_5,
  output [4:0] out_6,
  output [31:0] out_7,
  output [31:0] out_8,
  output [31:0] out_9
);

  Register #(.width(5)) register_1 (.D(in_1), .en(1'b1), .clk(in_5), .Q(out_6));  // open: clr
  Register #(.width(32)) register_2 (.D(in_2), .en(1'b1), .clk(in_5), .Q(out_7));  // open: clr
  Register #(.width(32)) register_3 (.D(in_3), .en(1'b1), .clk(in_5), .Q(out_8));  // open: clr
  Register #(.width(32)) register_4 (.D(in_4), .en(1'b1), .clk(in_5), .Q(out_9));  // open: clr
endmodule

module Reg_EXME (
  input  [31:0] in_1,
  input  [31:0] in_2,
  input  [4:0] in_3,
  input  in_4,
  output [31:0] out_5,
  output [31:0] out_6,
  output [4:0] out_7
);

  Register #(.width(32)) register_1 (.D(in_1), .en(1'b1), .clk(in_4), .Q(out_5));  // open: clr
  Register #(.width(32)) register_2 (.D(in_2), .en(1'b1), .clk(in_4), .Q(out_6));  // open: clr
  Register #(.width(5)) register_3 (.D(in_3), .en(1'b1), .clk(in_4), .Q(out_7));  // open: clr
endmodule

module Reg_MEWB (
  input  [4:0] in_1,
  input  in_2,
  input  [31:0] in_3,
  input  in_4,
  output [4:0] out_5,
  output [31:0] out_6
);

  wire [4:0] demultiplexer_1_out0, demultiplexer_1_out1, register_1_q, register_2_q, register_4_q;

  Demultiplexer #(.width(5), .enable("false")) demultiplexer_1 (
    .out0(demultiplexer_1_out0), .out1(demultiplexer_1_out1), .in(in_1), .sel(in_2));
  Register #(.width(5)) register_1 (.D(demultiplexer_1_out0), .en(1'b1), .clk(in_4), .Q(register_1_q));  // open: clr
  Register #(.width(5)) register_2 (.D(demultiplexer_1_out1), .en(1'b1), .clk(in_4), .Q(register_2_q));  // open: clr
  Register #(.width(32)) register_3 (.D(in_3), .en(1'b1), .clk(in_4), .Q(out_6));  // open: clr
  Register #(.width(5)) register_4 (.D(register_2_q), .en(1'b1), .clk(in_4), .Q(register_4_q));  // open: clr
  assign out_5 = register_1_q | register_4_q;  // OR_Gate or_1, 5 bits wide
endmodule

module Reg_2x (
  input  [1:0] in_1,
  input  Clock,
  output [1:0] out_3
);

  Register #(.width(2)) register_1 (.D(in_1), .en(1'b1), .clk(Clock), .Q(out_3));  // open: clr
endmodule

module Reg_4x (
  input  [3:0] in_1,
  input  in_2,
  output [3:0] out_3
);

  Register #(.width(4)) register_1 (.D(in_1), .en(1'b1), .clk(in_2), .Q(out_3));  // open: clr
endmodule

module Reg_1x (
  input  in_1,
  input  Clock,
  output out_3
);

  Register #(.width(1)) register_1 (.D(in_1), .en(1'b1), .clk(Clock), .Q(out_3));  // open: clr
endmodule

module Reg_3x (
  input  [2:0] in_1,
  input  Clock,
  output [2:0] out_3
);

  Register #(.width(3)) register_1 (.D(in_1), .en(1'b1), .clk(Clock), .Q(out_3));  // open: clr
endmodule
