// Logisim project 32BitCPU_x2.circ as structural Verilog: 5 circuits, main circuit main
module main (
);

  wire ASel, BSel, PCSel, RegEn, SysClk;
  wire [4:0] AddrA, AddrB, AddrD;
  wire [15:0] adder_1_out, bit_extender_1_out, multiplexer_1_out, PC;
  wire [31:0] ALUout, dataA, dataB, imem_1_instruction, multiplexer_2_out, multiplexer_3_out, PC32, undriven;

  Adder #(.width(16)) adder_1 (.a(PC), .b(16'h1), .out(adder_1_out));  // open: cin, cout
  Bit_Extender #(.in_width(32)) bit_extender_1 (.in(ALUout), .out(bit_extender_1_out));
  Register #(.width(16)) register_1 (.D(multiplexer_1_out), .en(1'b1), .clk(SysClk), .Q(PC));  // open: clr
  assign PC32 = {{16{PC[15]}}, PC};  // Bit_Extender bit_extender_2
  Multiplexer #(.width(16), .enable("false")) multiplexer_1 (
    .in0(adder_1_out), .in1(bit_extender_1_out), .out(multiplexer_1_out), .sel(PCSel));
  Clock clock_1 (.out(SysClk));
  iMem imem_1 (
    .PCVal(PC),
    .Instruction({imem_1_instruction[31:25], AddrB, AddrA, imem_1_instruction[14:12], AddrD, imem_1_instruction[6:0]}));
  regFile regfile_1 (
    .Clock(SysClk), .RegWEn(RegEn), .rs1(AddrA), .rs2(AddrB), .rd(AddrD), .data(undriven), .ReadData2(dataB),
    .ReadData1(dataA));  // open: spVal, t1Val, s0Val, a0Val, raVal, t0Val, t2Val, s1Val
  Multiplexer #(.width(32), .enable("false")) multiplexer_2 (
    .in0(dataA), .in1(PC32), .out(multiplexer_2_out), .sel(ASel));
  Multiplexer #(.width(32), .enable("false")) multiplexer_3 (
    .in0(dataB), .out(multiplexer_3_out), .sel(BSel));  // open: in1
  ALU alu_1 (.A(multiplexer_2_out), .B(multiplexer_3_out), .Result(ALUout));  // open: ALUSel
endmodule

module ALU (
  input  [31:0] A,
  input  [31:0] B,
  input  [31:0] Result,
  input  [3:0] ALUSel
);

  wire comparator_1_lt;
  wire [4:0] bit_extender_1_out, bit_extender_2_out, bit_extender_3_out;
  wire [30:0] bit_extender_4_out, bit_extender_5_out;
  wire [30:1] multiplier_1_cout;
  wire [31:0] adder_1_out, and_1_out, bit_extender_6_out, bit_extender_7_out, divider_1_out, divider_1_rem,
       multiplier_1_out, or_1_out, shifter_1_out, shifter_2_out, shifter_3_out, subtractor_1_out, xor_1_out;

  Bit_Extender #(.in_width(32), .out_width(5)) bit_extender_1 (.in(B), .out(bit_extender_1_out));
  Bit_Extender #(.in_width(32), .out_width(5)) bit_extender_2 (.in(B), .out(bit_extender_2_out));
  Bit_Extender #(.in_width(32), .out_width(5)) bit_extender_3 (.in(B), .out(bit_extender_3_out));
  Bit_Extender #(.in_width(32), .out_width(31)) bit_extender_4 (.in(A), .out(bit_extender_4_out));
  Bit_Extender #(.in_width(32), .out_width(31)) bit_extender_5 (.in(B), .out(bit_extender_5_out));
  Comparator #(.width(32)) comparator_1 (.a(A), .b(B), .lt(comparator_1_lt));  // open: gt, eq
  Multiplier #(.width(31)) multiplier_1 (
    .a(bit_extender_4_out), .b(bit_extender_5_out), .out(multiplier_1_out[30:0]),
    .cout({multiplier_1_cout, multiplier_1_out[31]}));  // open: cin
  Adder #(.width(32)) adder_1 (.a(A), .b(B), .out(adder_1_out));  // open: cin, cout
  assign and_1_out = A & B;  // AND_Gate and_1, 32 bits wide
  assign or_1_out = A | B;  // OR_Gate or_1, 32 bits wide
  assign xor_1_out = A ^ B;  // XOR_Gate xor_1, 32 bits wide
  Shifter #(.width(32), .shift("lr")) shifter_1 (.in(A), .\dist (bit_extender_1_out), .out(shifter_1_out));
  Shifter #(.width(32), .shift("ar")) shifter_2 (.in(A), .\dist (bit_extender_2_out), .out(shifter_2_out));
  Shifter #(.width(32)) shifter_3 (.in(A), .\dist (bit_extender_3_out), .out(shifter_3_out));
  assign bit_extender_6_out = {{31{comparator_1_lt}}, comparator_1_lt};  // Bit_Extender bit_extender_6
  Divider #(.width(32)) divider_1 (.a(A), .b(B), .out(divider_1_out), .rem(divider_1_rem));  // open: upper
  assign bit_extender_7_out = {{2{multiplier_1_cout[30]}}, multiplier_1_cout};  // Bit_Extender bit_extender_7
  Subtractor #(.width(32)) subtractor_1 (.a(A), .b(B), .out(subtractor_1_out));  // open: bin, bout
  Multiplexer #(.select(4), .width(32), .enable("false")) multiplexer_1 (
    .in0(adder_1_out), .in1(and_1_out), .in2(or_1_out), .in3(xor_1_out), .in4(shifter_1_out),
    .in5(shifter_2_out), .in6(shifter_3_out), .in7(bit_extender_6_out), .in8(divider_1_out),
    .in9(divider_1_rem), .in10(multiplier_1_out), .in11(bit_extender_7_out), .in12(subtractor_1_out),
    .in13(B), .out(Result), .sel(ALUSel));  // open: in14, in15
endmodule

module regFile (
  input  Clock,
  input  RegWEn,
  input  [4:0] rs1,
  input  [4:0] rs2,
  input  [4:0] rd,
  input  [31:0] data,
  output [31:0] ReadData1,
  output [31:0] ReadData2,
  output [31:0] raVal,
  output [31:0] spVal,
  output [31:0] t0Val,
  output [31:0] t1Val,
  output [31:0] t2Val,
  output [31:0] s0Val,
  output [31:0] s1Val,
  output [31:0] a0Val
);

  wire wr2, wr3, wr4, wr5, wr6, wr7, wr8, wr9;
  wire [31:0] x0;

  Demultiplexer #(.select(5), .enable("false")) demultiplexer_1 (
    .out1(wr2), .out2(wr3), .out5(wr4), .out6(wr5), .out7(wr6), .out8(wr7), .out9(wr8), .out10(wr9),
    .in(1'b1), .sel(rd));  // open: out0, out3, out4, out11, out12, out13, out14, out15, out16, out17, out18, out19, out20, out21, out22, out23, out24, out25, out26, out27, out28, out29, out30, out31
  Register #(.width(32)) register_1 (.D(data), .en(1'b0), .clk(Clock), .Q(x0));  // open: clr
  Register #(.width(32)) register_2 (.D(data), .en(wr4), .clk(Clock), .Q(t0Val));  // open: clr
  Register #(.width(32)) register_3 (.D(data), .en(wr7), .clk(Clock), .Q(s0Val));  // open: clr
  Register #(.width(32)) register_4 (.D(data), .en(wr2), .clk(Clock), .Q(raVal));  // open: clr
  Register #(.width(32)) register_5 (.D(data), .en(wr5), .clk(Clock), .Q(t1Val));  // open: clr
  Register #(.width(32)) register_6 (.D(data), .en(wr8), .clk(Clock), .Q(s1Val));  // open: clr
  Multiplexer #(.select(5), .width(32), .enable("false")) multiplexer_1 (
    .in0(x0), .in1(raVal), .in2(spVal), .in5(t0Val), .in6(t1Val), .in7(t2Val), .in8(s0Val), .in9(s1Val),
    .in10(a0Val), .out(ReadData1), .sel(rs1));  // open: in3, in4, in11, in12, in13, in14, in15, in16, in17, in18, in19, in20, in21, in22, in23, in24, in25, in26, in27, in28, in29, in30, in31
  Register #(.width(32)) register_7 (.D(data), .en(wr3), .clk(Clock), .Q(spVal));  // open: clr
  Register #(.width(32)) register_8 (.D(data), .en(wr6), .clk(Clock), .Q(t2Val));  // open: clr
  Register #(.width(32)) register_9 (.D(data), .en(wr9), .clk(Clock), .Q(a0Val));  // open: clr
  Multiplexer #(.select(5), .width(32), .enable("false")) multiplexer_2 (
    .in0(x0), .in1(raVal), .in2(spVal), .in5(t0Val), .in6(t1Val), .in7(t2Val), .in8(s0Val), .in9(s1Val),
    .in10(a0Val), .out(ReadData2), .sel(rs2));  // open: in3, in4, in11, in12, in13, in14, in15, in16, in17, in18, in19, in20, in21, in22, in23, in24, in25, in26, in27, in28, in29, in30, in31

  // Other names for the same wires on the sheet: regClk = Clock; regDataWrite[31:0] = data; regRDSelect[4:0] = rd;
  //   regRS1Select[4:0] = rs1; regRS2Select[4:0] = rs2; RS1Data[31:0] = ReadData1; RS2Data[31:0] = ReadData2;
  //   x1[31:0] = raVal; x2[31:0] = spVal; x5[31:0] = t0Val; x6[31:0] = t1Val; x7[31:0] = t2Val; x8[31:0] = s0Val;
  //   x9[31:0] = s1Val; x10[31:0] = a0Val

  // Notes on the sheet:
  //   INPUTS
  //   OUTPUTS
endmodule

module iMem (
  input  [15:0] PCVal,
  output [31:0] Instruction
);

  ROM #(.addrWidth(16), .dataWidth(32)) rom_1 (.addr(PCVal), .data(Instruction));
endmodule

module controlPath (
  input  in_1,
  input  in_2,
  input  [31:0] Instruction,
  output PCSel,
  output [2:0] ImmSel,
  output BrUn,
  output ASel,
  output BSel,
  output [3:0] ALUSel,
  output MemRW,
  output RegWEn,
  output [1:0] WBSel
);

  wire [7:0] adder_1_out, bit_extender_1_out, bit_extender_2_out;
  wire [15:15] rom_1_data;

  assign bit_extender_1_out = {{1{Instruction[6]}}, Instruction[6:0]};  // Bit_Extender bit_extender_1
  assign bit_extender_2_out = {{5{Instruction[14]}}, Instruction[14:12]};  // Bit_Extender bit_extender_2
  Adder adder_1 (.a(bit_extender_1_out), .b(bit_extender_2_out), .out(adder_1_out));  // open: cin, cout
  ROM #(.dataWidth(16)) rom_1 (
    .addr(adder_1_out), .data({rom_1_data[15], PCSel, ImmSel, BrUn, ASel, BSel, ALUSel, MemRW, RegWEn, WBSel}));
  Bit_Extender #(.in_width(3), .out_width(8), .\type ("zero")) bit_extender_3 (.in(Instruction[14:12]));  // open: out

  // Other names for the same wires on the sheet: BrEq = in_1; BrLt = in_2; func3[2:0] = Instruction[14:12];
  //   inst[31:0] = Instruction; opcode[6:0] = Instruction[6:0]

  // Notes on the sheet:
  //   contents of rom_1 (hex, n*v repeats v):
  //   0 0 0 ffff
endmodule
